// Logisim project 8bitsubadder.circ as structural Verilog: 3 circuits, main circuit main
module main (
  input  [7:0] in_1,
  input  in_2,
  input  [7:0] in_3,
  output [7:0] out_4
);

  wire full_adder_2_out_4, full_adder_3_out_4, full_adder_4_out_4, full_adder_5_out_4, full_adder_6_out_4,
       full_adder_7_out_4, full_adder_8_out_4;
  wire [7:0] not_1_out;

  full_adder full_adder_1 (
    .in_1(in_1[7]), .in_2(not_1_out[7]), .in_3(full_adder_2_out_4), .out_5(out_4[7]));  // open: out_4
  full_adder full_adder_2 (
    .in_1(in_1[6]), .in_2(not_1_out[6]), .in_3(full_adder_3_out_4), .out_4(full_adder_2_out_4),
    .out_5(out_4[6]));
  full_adder full_adder_3 (
    .in_1(in_1[5]), .in_2(not_1_out[5]), .in_3(full_adder_4_out_4), .out_4(full_adder_3_out_4),
    .out_5(out_4[5]));
  full_adder full_adder_4 (
    .in_1(in_1[4]), .in_2(not_1_out[4]), .in_3(full_adder_5_out_4), .out_4(full_adder_4_out_4),
    .out_5(out_4[4]));
  full_adder full_adder_5 (
    .in_1(in_1[3]), .in_2(not_1_out[3]), .in_3(full_adder_6_out_4), .out_4(full_adder_5_out_4),
    .out_5(out_4[3]));
  full_adder full_adder_6 (
    .in_1(in_1[2]), .in_2(not_1_out[2]), .in_3(full_adder_7_out_4), .out_4(full_adder_6_out_4),
    .out_5(out_4[2]));
  full_adder full_adder_7 (
    .in_1(in_1[1]), .in_2(not_1_out[1]), .in_3(full_adder_8_out_4), .out_4(full_adder_7_out_4),
    .out_5(out_4[1]));
  full_adder full_adder_8 (
    .in_1(in_1[0]), .in_2(not_1_out[0]), .in_3(in_2), .out_4(full_adder_8_out_4), .out_5(out_4[0]));
  assign not_1_out = ~in_3;  // NOT_Gate not_1, 8 bits wide
endmodule

module half_adder (
  input  in_1,
  input  in_2,
  output out_3,
  output out_4
);

  and and_1 (out_3, in_1, in_2);
  xor xor_1 (out_4, in_1, in_2);
endmodule

module full_adder (
  input  in_1,
  input  in_2,
  input  in_3,
  output out_4,
  output out_5
);

  wire half_adder_1_out_3, half_adder_1_out_4, half_adder_2_out_3;

  half_adder half_adder_1 (.in_1(in_1), .in_2(in_2), .out_3(half_adder_1_out_3), .out_4(half_adder_1_out_4));
  or or_1 (out_4, half_adder_1_out_3, half_adder_2_out_3);
  half_adder half_adder_2 (.in_1(half_adder_1_out_4), .in_2(in_3), .out_3(half_adder_2_out_3), .out_4(out_5));
endmodule
