// Logisim project DanielRossoT1CircuitosDigitais.circ as structural Verilog: 2 circuits, main circuit BLOCK
module main (
  input  A,
  input  B,
  input  C,
  input  D,
  output b_2,
  output c_2,
  output d_2,
  output e,
  output f,
  output a_2,
  output g
);

  wire and_2_out, and_3_out, and_4_out, and_5_out, and_6_out, and_7_out, and_8_out, and_9_out, and_10_out,
       and_11_out, and_12_out, and_13_out, and_14_out, and_15_out, and_16_out, and_17_out, and_18_out,
       and_19_out, not_1_out, not_2_out, not_3_out, not_4_out;

  not not_1 (not_1_out, A);
  not not_2 (not_2_out, B);
  not not_3 (not_3_out, C);
  not not_4 (not_4_out, D);
  and and_1 (b_2, not_1_out, not_2_out, not_3_out);
  and and_2 (and_2_out, not_1_out, B, C, D);
  and and_3 (and_3_out, not_2_out, not_3_out);
  and and_4 (and_4_out, not_2_out, not_4_out);
  and and_5 (and_5_out, not_1_out, B, D);
  and and_6 (and_6_out, not_1_out, not_3_out, not_4_out);
  and and_7 (and_7_out, A, not_2_out, not_3_out);
  and and_8 (and_8_out, A, not_2_out, not_4_out);
  and and_9 (and_9_out, not_2_out, C, not_4_out);
  and and_10 (and_10_out, not_1_out, not_2_out, D);
  and and_11 (and_11_out, not_1_out, B, not_3_out);
  and and_12 (and_12_out, A, not_2_out, not_3_out);
  and and_13 (and_13_out, not_1_out, B, not_3_out, not_4_out);
  and and_14 (and_14_out, A, not_2_out, not_3_out);
  and and_15 (and_15_out, not_2_out, not_3_out, D);
  and and_16 (and_16_out, not_1_out, B, C);
  and and_17 (and_17_out, not_2_out, not_3_out);
  and and_18 (and_18_out, not_2_out, not_4_out);
  and and_19 (and_19_out, not_1_out, not_4_out);
  or or_1 (c_2, and_2_out, and_3_out, and_4_out);
  or or_2 (d_2, and_5_out, and_6_out, and_7_out, and_8_out);
  or or_3 (e, and_9_out, not_1_out);
  or or_4 (f, and_10_out, and_11_out, and_12_out);
  or or_5 (a_2, and_13_out, and_14_out, and_15_out);
  or or_6 (g, and_16_out, and_17_out, and_18_out, and_19_out);
endmodule

module BLOCK (
  input  in_1,
  input  in_2,
  input  in_3,
  input  in_4
);

  wire main_1_a_2, main_1_b_2, main_1_c_2, main_1_d_2, main_1_e, main_1_f, main_1_g;

  main main_1 (
    .A(in_1), .D(in_4), .B(in_2), .b_2(main_1_b_2), .c_2(main_1_c_2), .d_2(main_1_d_2), .e(main_1_e),
    .f(main_1_f), .a_2(main_1_a_2), .g(main_1_g), .C(in_3));
  _7_Segment_Display u_7_segment_display_1 (
    .g(main_1_g), .f(main_1_f), .a(main_1_a_2), .b(main_1_b_2), .e(main_1_e), .d(main_1_d_2), .c(main_1_c_2));  // open: dp
endmodule
