// Logisim project comparadorDobrado.circ as structural Verilog: 1 circuit, main circuit main
module main (
  input  [2:0] in_1,
  input  in_2,
  input  in_3,
  input  in_4,
  input  in_5,
  output [7:0] out_6,
  output [7:0] out_7
);

  wire and_1_out, and_2_out;

  and and_1 (and_1_out, in_2, ~in_3);  // AND_Gate
  and and_2 (and_2_out, in_2, in_3);
  Decoder #(.select(2), .disabled(0)) decoder_1 (
    .out0(out_6[0]), .out1(out_6[1]), .out2(out_6[2]), .out3(out_6[3]), .sel({in_4, in_5}), .en(and_1_out));
  Decoder #(.select(2), .disabled(0)) decoder_2 (
    .out0(out_6[4]), .out1(out_6[5]), .out2(out_6[6]), .out3(out_6[7]), .sel({in_4, in_5}), .en(and_2_out));
  Decoder #(.select(3), .enable("false")) decoder_3 (
    .out0(out_7[0]), .out1(out_7[1]), .out2(out_7[2]), .out3(out_7[3]), .out4(out_7[4]), .out5(out_7[5]),
    .out6(out_7[6]), .out7(out_7[7]), .sel(in_1));
endmodule
