// Logisim project danielrossom2t2.circ as structural Verilog: 5 circuits, main circuit main
module main (
  input  in_1,
  input  in_2,
  input  in_3,
  input  in_4,
  input  in_5,
  input  in_6,
  input  in_7,
  input  in_8,
  input  in_9,
  input  in_10,
  input  in_11,
  output out_12,
  output out_13,
  output out_14,
  output out_15,
  output out_16,
  output out_17,
  output out_18,
  output out_19,
  output out_20
);

  wire nor_1_out, nor_2_out, nor_3_out;
  wire [3:3] and_1_out, and_2_out, and_3_out;

  Hex_Digit_Display hex_digit_display_1 (.value({and_1_out[3], in_2, in_3, in_4}));  // open: dp
  Hex_Digit_Display hex_digit_display_2 (.value({and_2_out[3], out_18, out_19, out_20}));  // open: dp
  and and_1 (and_1_out[3], in_1, nor_1_out);
  ula ula_1 (
    .ov(out_14), .ZF(out_15), .in_5(in_8), .A(in_7), .in_7(in_6), .in_8(in_5), .in_1(in_4), .B(in_3),
    .in_3(in_2), .in_4(in_1), .s(in_9), .in_10(in_10), .in_11(in_11), .out_14(out_16), .out_15(out_18),
    .o(out_19), .out_17(out_20));
  and and_2 (and_2_out[3], nor_2_out, out_16);
  nor nor_1 (nor_1_out, in_2, in_3, in_4);
  nor nor_2 (nor_2_out, out_18, out_19, out_20);
  and and_3 (and_3_out[3], in_5, nor_3_out);
  nor nor_3 (nor_3_out, in_6, in_7, in_8);
  Hex_Digit_Display hex_digit_display_3 (.value({and_3_out[3], in_6, in_7, in_8}));  // open: dp

  assign out_12 = in_1;
  assign out_13 = in_5;
  assign out_17 = out_16;

  // Notes on the sheet:
  //   000 INC A
  //   001 DEC A
  //   010 ADD A, B
  //   011 ADD A, -B
  //   100 NOT A
  //   101 OR A, B
  //   110 AND A,B
  //   111 XOR A,B
endmodule

module half_adder (
  input  in_1,
  input  in_2,
  output out_3,
  output out_4
);

  and and_1 (out_3, in_1, in_2);
  xor xor_1 (out_4, in_1, in_2);
endmodule

module full_adder (
  input  in_1,
  input  in_2,
  input  in_3,
  output out_4,
  output out_5
);

  wire half_adder_1_out_3, half_adder_1_out_4, half_adder_2_out_3;

  half_adder half_adder_1 (.in_1(in_1), .in_2(in_2), .out_3(half_adder_1_out_3), .out_4(half_adder_1_out_4));
  or or_1 (out_4, half_adder_1_out_3, half_adder_2_out_3);
  half_adder half_adder_2 (.in_1(half_adder_1_out_4), .in_2(in_3), .out_3(half_adder_2_out_3), .out_4(out_5));
endmodule

module _4bitaddersubber (
  input  [3:0] in_1,
  input  in_2,
  input  [3:0] in_3,
  output out_4,
  output [3:0] out_5
);

  wire full_adder_1_out_4, full_adder_2_out_4, full_adder_3_out_4, full_adder_4_out_4;
  wire [3:0] xor_5_out;

  xor xor_1 (out_4, full_adder_1_out_4, full_adder_2_out_4);
  full_adder full_adder_1 (
    .in_1(in_1[3]), .in_2(xor_5_out[3]), .in_3(full_adder_2_out_4), .out_4(full_adder_1_out_4),
    .out_5(out_5[3]));
  full_adder full_adder_2 (
    .in_1(in_1[2]), .in_2(xor_5_out[2]), .in_3(full_adder_3_out_4), .out_4(full_adder_2_out_4),
    .out_5(out_5[2]));
  full_adder full_adder_3 (
    .in_1(in_1[1]), .in_2(xor_5_out[1]), .in_3(full_adder_4_out_4), .out_4(full_adder_3_out_4),
    .out_5(out_5[1]));
  full_adder full_adder_4 (
    .in_1(in_1[0]), .in_2(xor_5_out[0]), .in_3(in_2), .out_4(full_adder_4_out_4), .out_5(out_5[0]));
  xor xor_2 (xor_5_out[3], in_3[3], in_2);
  xor xor_3 (xor_5_out[2], in_3[2], in_2);
  xor xor_4 (xor_5_out[1], in_3[1], in_2);
  xor xor_5 (xor_5_out[0], in_3[0], in_2);
endmodule

module ula (
  input  in_1,
  input  B,
  input  in_3,
  input  in_4,
  input  in_5,
  input  A,
  input  in_7,
  input  in_8,
  input  s,
  input  in_10,
  input  in_11,
  output ov,
  output ZF,
  output out_14,
  output out_15,
  output o,
  output out_17
);

  wire not_1_out, or_1_out;
  wire [3:0] and_1_out, multiplexer_1_out, n4bitaddersubber_1_out_5, not_3_out, or_2_out, xor_1_out;

  not not_1 (not_1_out, in_11);
  not not_2 (ZF, or_1_out);
  Multiplexer #(.select(2), .width(4)) multiplexer_1 (
    .in0(4'b0001), .in1(4'b0001), .in2({in_4, in_3, B, in_1}), .in3({in_4, in_3, B, in_1}),
    .out(multiplexer_1_out), .sel({in_10, s}), .en(not_1_out));
  or or_1 (or_1_out, out_17, o, out_15, out_14);
  _4bitaddersubber u_4bitaddersubber_1 (
    .in_2(s), .in_1({in_8, in_7, A, in_5}), .out_5(n4bitaddersubber_1_out_5), .in_3(multiplexer_1_out),
    .out_4(ov));
  Multiplexer #(.select(3), .width(4), .enable("false")) multiplexer_2 (
    .in0(n4bitaddersubber_1_out_5), .in1(n4bitaddersubber_1_out_5), .in2(n4bitaddersubber_1_out_5),
    .in3(n4bitaddersubber_1_out_5), .in4(not_3_out), .in5(or_2_out), .in6(and_1_out), .in7(xor_1_out),
    .out({out_14, out_15, o, out_17}), .sel({in_11, in_10, s}));
  assign not_3_out = ~{in_8, in_7, A, in_5};  // NOT_Gate not_3, 4 bits wide
  assign and_1_out = {in_8, in_7, A, in_5} & {in_4, in_3, B, in_1};  // AND_Gate and_1, 4 bits wide
  assign or_2_out = {in_8, in_7, A, in_5} | {in_4, in_3, B, in_1};  // OR_Gate or_2, 4 bits wide
  assign xor_1_out = {in_8, in_7, A, in_5} ^ {in_4, in_3, B, in_1};  // XOR_Gate xor_1, 4 bits wide
endmodule
